# Fritzing sketch schematic (saved by Fritzing 0.9.2b)
breadboards: 1

parts:
  D1 = Rectifier Diode [part_number=1N4001 package="300 mil [THT]"]
  D2 = Rectifier Diode [part_number=1N4001 package="300 mil [THT]"]
  D3 = Rectifier Diode [part_number=1N4001 package="300 mil [THT]"]
  D4 = Rectifier Diode [part_number=1N4001 package="300 mil [THT]"]
  C1 = Electrolytic Capacitor [capacitance=1µF package="100 mil [THT, electrolytic]"]
  V1 = AC Power [voltage=5 frequency=60]
  V2 = AC Power [voltage=20 frequency=60]
  C2 = Capacitor Polarized [package=nippon_f80]
  R1 = Resistor [tolerance=±5% resistance=3.6k package="0805 [SMD]"]
  R2 = Resistor [tolerance=±5% resistance=1.2k package="0805 [SMD]"]
  U1 = Optocoupler [part_number=4N33 package=THT]
  V3 = DC Power [voltage=3.3V]
  D5 = Diode [package=diode-1n4001]
  R3 = Resistor [tolerance=±5% resistance=220 package="0805 [SMD]"]
  Part1 = Spark Core (v1.0)
  U2 = LMZ14203 [package=to-pmod-7]

nets:
  N1: D1.cathode, D2.anode, V1.V+
  GND: D1.anode, D3.anode, C1.-, Part1.GND, U2.GND
  N2: D2.cathode, D4.cathode, C1.+, U2.VIN
  N3: D3.cathode, D4.anode, V1.V-
  N4: V2.V+, D5.A
  N5: C2.-, R2.Pin_1, U1.Pin_2
  N6: R1.Pin_0, D5.C
  N7: R1.Pin_1, R2.Pin_0, U1.Pin_1
  GND_2: U1.Pin_4
  N8: U1.Pin_5, R3.Pin_1, Part1.D4
  N9: V3.V-, R3.Pin_0
  N10: Part1.VIN, U2.VOUT

notes:
  This is just a half wave rectifier into a resistor divider to step voltage down to about 5v. you want only enough current to trigger your optocoupler, so look at the datasheet and then pick resistor values appropriately
  this is just a bridge rectifier into a DC DC stepdown. take 20v down to 5v to power the Spark. pick whatever you want.
